# Fritzing sketch arduino_uno_pn532_spi (saved by Fritzing 1.0.6)

parts:
  Composant2 = PN532 Elechouse RFID NFC Module V3
  A1 = Arduino UNO R4 WiFi

nets:
  N1: Composant2.GND, A1.Pin_9, A1.Pin_18
  N2: Composant2.VCC, A1.Pin_7, A1.Pin_19
  N3: Composant2.SCK, A1.Pin_47
  N4: Composant2.MISO, A1.Pin_46
  N5: Composant2.MOSI, A1.Pin_45
  N6: Composant2.SS, A1.Pin_44

custom parts:
  PN532 Elechouse RFID NFC Module V3: NFC is a popular technology in recent years. We often heard this work while smart phone company such as Samsung or HTC introduces their latest high-end phones. Almost all the high-end phone in the market support NFC. Near field communication (NFC) is a set of standards for smart phones and similar devices to establish radio communication with each other by touching them together or bringing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
  Arduino UNO R4 WiFi: The Arduino UNO R4 WiFi merges the RA4M1 microprocessor from Renesas with the ESP32-S3 from Espressif, creating an all-in-one tool for makers with enhanced processing power and a diverse array of new peripherals.
